// Logisim project T.Chen CPU.circ as structural Verilog: 4 circuits, main circuit implementation
module implementation (
  input  [15:0] Instruction_In,
  input  Clk,
  output [4:0] Instruction_Address_Out,
  output [3:0] out_4,
  output [3:0] Reg0_Out,
  output [3:0] Reg1_Out,
  output [3:0] Reg2_Out,
  output [3:0] out_8,
  output [3:0] Reg3_Out,
  output [3:0] out_10,
  output [3:0] Reg4_Out,
  output [3:0] Reg5_Out,
  output [3:0] Reg6_Out,
  output [3:0] out_14,
  output [3:0] Reg7_Out,
  output [3:0] Reg8_Out,
  output [3:0] Reg9_Out,
  output [3:0] Reg10_Out,
  output [3:0] out_19,
  output [3:0] Reg11_Out,
  output [3:0] Reg12_Out,
  output [3:0] Reg13_Out,
  output [3:0] Reg14_Out,
  output [3:0] Reg15_Out
);

  wire is_continune, is_immediate, is_regist_write;
  wire [3:0] A_Value, ALU_out, B_Value, multiplexer_1_out;
  wire [4:0] adder_1_out;

  Register #(.width(5)) register_1 (
    .D(adder_1_out), .en(is_continune), .clk(Clk), .Q(Instruction_Address_Out));  // open: clr
  Decode decode_1 (
    .opCode_In(Instruction_In[15:12]), .Is_rewrite(is_regist_write), .Is_Immediate(is_immediate),
    .Is_continune(is_continune));
  Adder #(.width(5)) adder_1 (.a(5'b00010), .b(Instruction_Address_Out), .out(adder_1_out));  // open: cin, cout
  Multiplexer #(.enable("false"), .width(4)) multiplexer_1 (
    .in0(B_Value), .in1(Instruction_In[3:0]), .out(multiplexer_1_out), .sel(is_immediate));
  ALU alu_1 (.RegA_In(A_Value), .RegB_In(multiplexer_1_out), .OPCode_In(Instruction_In[15:12]), .ALU_output(ALU_out));
  RegFile regfile_1 (
    .A_Sel_In(Instruction_In[7:4]), .B_Sel_In(Instruction_In[3:0]), .C_Sel_In(Instruction_In[11:8]),
    .Data_In(ALU_out), .Reg_Write_In(is_regist_write), .clk_in(Clk), .A_Out(A_Value), .B_Out(B_Value),
    .Reg0_Out(Reg0_Out), .Reg1_Out(Reg1_Out), .Reg2_Out(Reg2_Out), .Reg3_Out(Reg3_Out), .Reg4_Out(Reg4_Out),
    .Reg5_Out(Reg5_Out), .Reg6_Out(Reg6_Out), .Reg7_Out(Reg7_Out), .Reg8_Out(Reg8_Out), .Reg9_Out(Reg9_Out),
    .Reg10_Out(Reg10_Out), .Reg11_Out(Reg11_Out), .Reg12_Out(Reg12_Out), .Reg13_Out(Reg13_Out),
    .Reg14_Out(Reg14_Out), .Reg15_Out(Reg15_Out));

  assign out_4 = Instruction_In[3:0];
  assign out_8 = Instruction_In[7:4];
  assign out_10 = Instruction_In[11:8];
  assign out_14 = Instruction_In[15:12];
  assign out_19 = Instruction_In[15:12];

  // Other names for the same wires on the sheet: Instruction[15:0] = Instruction_In; RegB[3:0] = Instruction_In[3:0];
  //   RegA[3:0] = Instruction_In[7:4]; RegC[3:0] = Instruction_In[11:8]; Opcode[3:0] = Instruction_In[15:12];
  //   Instruction_Address[4:0] = Instruction_Address_Out; Reg0[3:0] = Reg0_Out; Reg1[3:0] = Reg1_Out;
  //   Reg2[3:0] = Reg2_Out; Reg3[3:0] = Reg3_Out; Reg4[3:0] = Reg4_Out; Reg5[3:0] = Reg5_Out; Reg6[3:0] = Reg6_Out;
  //   Reg7[3:0] = Reg7_Out; Reg8[3:0] = Reg8_Out; Reg9[3:0] = Reg9_Out; Reg10[3:0] = Reg10_Out;
  //   Reg11[3:0] = Reg11_Out; Reg12[3:0] = Reg12_Out; Reg13[3:0] = Reg13_Out; Reg14[3:0] = Reg14_Out;
  //   Reg15[3:0] = Reg15_Out

  // Notes on the sheet:
  //   This is my PC and Alway increment by 2
endmodule

module RegFile (
  input  [3:0] A_Sel_In,
  input  [3:0] B_Sel_In,
  input  [3:0] C_Sel_In,
  input  [3:0] Data_In,
  input  Reg_Write_In,
  input  clk_in,
  output [3:0] A_Out,
  output [3:0] B_Out,
  output [3:0] Reg0_Out,
  output [3:0] Reg1_Out,
  output [3:0] Reg2_Out,
  output [3:0] Reg3_Out,
  output [3:0] Reg4_Out,
  output [3:0] Reg5_Out,
  output [3:0] Reg6_Out,
  output [3:0] Reg7_Out,
  output [3:0] Reg8_Out,
  output [3:0] Reg9_Out,
  output [3:0] Reg10_Out,
  output [3:0] Reg11_Out,
  output [3:0] Reg12_Out,
  output [3:0] Reg13_Out,
  output [3:0] Reg14_Out,
  output [3:0] Reg15_Out
);

  wire Reg_Write0, Reg_Write1, Reg_Write2, Reg_Write3, Reg_Write4, Reg_Write5, Reg_Write6, Reg_Write7,
       Reg_Write8, Reg_Write9, Reg_Write10, Reg_Write11, Reg_Write12, Reg_Write13, Reg_Write14, Reg_Write15;

  Demultiplexer #(.enable("false"), .select(4)) demultiplexer_1 (
    .out0(Reg_Write0), .out1(Reg_Write1), .out2(Reg_Write2), .out3(Reg_Write3), .out4(Reg_Write4),
    .out5(Reg_Write5), .out6(Reg_Write6), .out7(Reg_Write7), .out8(Reg_Write8), .out9(Reg_Write9),
    .out10(Reg_Write10), .out11(Reg_Write11), .out12(Reg_Write12), .out13(Reg_Write13), .out14(Reg_Write14),
    .out15(Reg_Write15), .in(Reg_Write_In), .sel(C_Sel_In));
  Register #(.width(4)) register_1 (.D(Data_In), .en(Reg_Write0), .clk(clk_in), .Q(Reg0_Out));  // open: clr
  Register #(.width(4)) register_2 (.D(Data_In), .en(Reg_Write4), .clk(clk_in), .Q(Reg4_Out));  // open: clr
  Register #(.width(4)) register_3 (.D(Data_In), .en(Reg_Write8), .clk(clk_in), .Q(Reg8_Out));  // open: clr
  Register #(.width(4)) register_4 (.D(Data_In), .en(Reg_Write12), .clk(clk_in), .Q(Reg12_Out));  // open: clr
  Register #(.width(4)) register_5 (.D(Data_In), .en(Reg_Write1), .clk(clk_in), .Q(Reg1_Out));  // open: clr
  Register #(.width(4)) register_6 (.D(Data_In), .en(Reg_Write5), .clk(clk_in), .Q(Reg5_Out));  // open: clr
  Register #(.width(4)) register_7 (.D(Data_In), .en(Reg_Write9), .clk(clk_in), .Q(Reg9_Out));  // open: clr
  Register #(.width(4)) register_8 (.D(Data_In), .en(Reg_Write13), .clk(clk_in), .Q(Reg13_Out));  // open: clr
  Register #(.width(4)) register_9 (.D(Data_In), .en(Reg_Write2), .clk(clk_in), .Q(Reg2_Out));  // open: clr
  Register #(.width(4)) register_10 (.D(Data_In), .en(Reg_Write6), .clk(clk_in), .Q(Reg6_Out));  // open: clr
  Register #(.width(4)) register_11 (.D(Data_In), .en(Reg_Write10), .clk(clk_in), .Q(Reg10_Out));  // open: clr
  Register #(.width(4)) register_12 (.D(Data_In), .en(Reg_Write14), .clk(clk_in), .Q(Reg14_Out));  // open: clr
  Register #(.width(4)) register_13 (.D(Data_In), .en(Reg_Write3), .clk(clk_in), .Q(Reg3_Out));  // open: clr
  Register #(.width(4)) register_14 (.D(Data_In), .en(Reg_Write7), .clk(clk_in), .Q(Reg7_Out));  // open: clr
  Register #(.width(4)) register_15 (.D(Data_In), .en(Reg_Write11), .clk(clk_in), .Q(Reg11_Out));  // open: clr
  Register #(.width(4)) register_16 (.D(Data_In), .en(Reg_Write15), .clk(clk_in), .Q(Reg15_Out));  // open: clr
  Multiplexer #(.enable("false"), .select(4), .width(4)) multiplexer_1 (
    .in0(Reg0_Out), .in1(Reg1_Out), .in2(Reg2_Out), .in3(Reg3_Out), .in4(Reg4_Out), .in5(Reg5_Out),
    .in6(Reg6_Out), .in7(Reg7_Out), .in8(Reg8_Out), .in9(Reg9_Out), .in10(Reg10_Out), .in11(Reg11_Out),
    .in12(Reg12_Out), .in13(Reg13_Out), .in14(Reg14_Out), .in15(Reg15_Out), .out(A_Out), .sel(A_Sel_In));
  Multiplexer #(.enable("false"), .select(4), .width(4)) multiplexer_2 (
    .in0(Reg0_Out), .in1(Reg1_Out), .in2(Reg2_Out), .in3(Reg3_Out), .in4(Reg4_Out), .in5(Reg5_Out),
    .in6(Reg6_Out), .in7(Reg7_Out), .in8(Reg8_Out), .in9(Reg9_Out), .in10(Reg10_Out), .in11(Reg11_Out),
    .in12(Reg12_Out), .in13(Reg13_Out), .in14(Reg14_Out), .in15(Reg15_Out), .out(B_Out), .sel(B_Sel_In));

  // Other names for the same wires on the sheet: A[3:0] = A_Out; A_Sel[3:0] = A_Sel_In; B[3:0] = B_Out;
  //   B_Sel[3:0] = B_Sel_In; C_Sel[3:0] = C_Sel_In; clk = clk_in; Data[3:0] = Data_In; Reg0[3:0] = Reg0_Out;
  //   Reg1[3:0] = Reg1_Out; Reg2[3:0] = Reg2_Out; Reg3[3:0] = Reg3_Out; Reg4[3:0] = Reg4_Out; Reg5[3:0] = Reg5_Out;
  //   Reg6[3:0] = Reg6_Out; Reg7[3:0] = Reg7_Out; Reg8[3:0] = Reg8_Out; Reg9[3:0] = Reg9_Out; Reg10[3:0] = Reg10_Out;
  //   Reg11[3:0] = Reg11_Out; Reg12[3:0] = Reg12_Out; Reg13[3:0] = Reg13_Out; Reg14[3:0] = Reg14_Out;
  //   Reg15[3:0] = Reg15_Out; Reg_Write = Reg_Write_In
endmodule

module Decode (
  input  [3:0] opCode_In,
  output Is_rewrite,
  output Is_Immediate,
  output Is_continune
);

  wire and_1_out, and_2_out, and_3_out, and_4_out, not_1_out, not_2_out, not_3_out;

  not not_1 (not_1_out, opCode_In[3]);
  not not_2 (not_2_out, opCode_In[2]);
  not not_3 (not_3_out, opCode_In[0]);
  or or_1 (Is_rewrite, opCode_In[1], opCode_In[2], opCode_In[3]);
  and and_1 (and_1_out, not_1_out, opCode_In[1], not_3_out);
  and and_2 (and_2_out, not_1_out, opCode_In[2], not_3_out);
  and and_3 (and_3_out, opCode_In[3], not_2_out, not_3_out);
  and and_4 (and_4_out, opCode_In[3], opCode_In[2], opCode_In[1], opCode_In[0]);
  or or_2 (Is_continune, opCode_In[1], opCode_In[2], opCode_In[3]);
  or or_3 (Is_Immediate, and_1_out, and_2_out, and_3_out, and_4_out);
endmodule

module ALU (
  input  [3:0] RegA_In,
  input  [3:0] RegB_In,
  input  [3:0] OPCode_In,
  output [3:0] ALU_output
);

  wire [3:0] adder_1_out, adder_2_out, and_1_out, and_2_out, negator_1_out, not_1_out, or_1_out, or_2_out,
       subtractor_1_out, subtractor_2_out, xor_1_out, xor_2_out;

  assign or_1_out = RegA_In | RegB_In;  // OR_Gate or_1, 4 bits wide
  assign xor_1_out = RegA_In ^ RegB_In;  // XOR_Gate xor_1, 4 bits wide
  assign xor_2_out = RegA_In ^ RegB_In;  // XOR_Gate xor_2, 4 bits wide
  Negator #(.width(4)) negator_1 (.in(RegA_In), .out(negator_1_out));
  assign not_1_out = ~RegA_In;  // NOT_Gate not_1, 4 bits wide
  assign or_2_out = RegA_In | RegB_In;  // OR_Gate or_2, 4 bits wide
  assign and_1_out = RegA_In & RegB_In;  // AND_Gate and_1, 4 bits wide
  Multiplexer #(.enable("false"), .select(4), .width(4)) multiplexer_1 (
    .in2(adder_1_out), .in3(adder_2_out), .in4(subtractor_2_out), .in5(subtractor_1_out), .in6(and_2_out),
    .in7(and_1_out), .in8(or_2_out), .in9(or_1_out), .in10(xor_1_out), .in11(xor_2_out),
    .in12(negator_1_out), .in13(not_1_out), .in14(RegA_In), .in15(RegB_In), .out(ALU_output), .sel(OPCode_In));  // open: in0, in1
  assign and_2_out = RegA_In & RegB_In;  // AND_Gate and_2, 4 bits wide
  Subtractor #(.width(4)) subtractor_1 (.a(RegA_In), .b(RegB_In), .out(subtractor_1_out));  // open: bin, bout
  Adder #(.width(4)) adder_1 (.a(RegA_In), .b(RegB_In), .out(adder_1_out));  // open: cin, cout
  Subtractor #(.width(4)) subtractor_2 (.a(RegA_In), .b(RegB_In), .out(subtractor_2_out));  // open: bin, bout
  Adder #(.width(4)) adder_2 (.a(RegA_In), .b(RegB_In), .out(adder_2_out));  // open: cin, cout

  // Other names for the same wires on the sheet: A[3:0] = RegA_In; B[3:0] = RegB_In; Op_selector[3:0] = OPCode_In
endmodule
