// Logisim project T.Chen_8BtisCache.circ as structural Verilog: 2 circuits, main circuit Implementation
module Implementation (
  input  [7:0] Address_Input,
  input  [7:0] CPU_Input,
  input  Write_Enable,
  input  Clk_in,
  output [4:0] Entry0,
  output [4:0] Entry1,
  output [4:0] Entry2,
  output [4:0] Entry3,
  output [4:0] Entry4,
  output [4:0] Entry5,
  output [4:0] Entry6,
  output [4:0] Entry7,
  output [7:0] out_13,
  output Valid_Bits_Entry0,
  output Dirty_Bits_Entry0,
  output Valid_Bits_Entry1,
  output Dirty_Bits_Entry1,
  output Valid_Bits_Entry2,
  output Dirty_Bits_Entry2,
  output Valid_Bits_Entry3,
  output DIrty_Bits_Entry3,
  output Valid_Bits_Entry4,
  output Dirty_Bits_Entry4,
  output Valid_Bits_Entry5,
  output Dirty_Bits_Entry5,
  output Valid_Bits_Entry6,
  output Dirty_Bits_Entry6,
  output Valid_Bits_Entry7,
  output Dirty_Bits_Entry7
);

  wire fetch_from_memory;
  wire [7:0] MEM_Data, multiplexer_1_out;

  Multiplexer #(.width(8)) multiplexer_1 (
    .in0(CPU_Input), .in1(MEM_Data), .out(multiplexer_1_out), .sel(fetch_from_memory));  // open: en
  EightBitsCache eightbitscache_1 (
    .Address_in(Address_Input), .Write_Enable(Write_Enable), .RAM_Write_Enable(fetch_from_memory),
    .clk_in(Clk_in), .Data_in(multiplexer_1_out),
    .Tag_out({Entry7, Entry6, Entry5, Entry4, Entry3, Entry2, Entry1, Entry0}), .Output_Data(out_13),
    .Is_Entry_Valid({Valid_Bits_Entry0, Valid_Bits_Entry1, Valid_Bits_Entry2, Valid_Bits_Entry3, Valid_Bits_Entry4, Valid_Bits_Entry5, Valid_Bits_Entry6, Valid_Bits_Entry7}),
    .Dirty_Status({Dirty_Bits_Entry0, Dirty_Bits_Entry1, Dirty_Bits_Entry2, DIrty_Bits_Entry3, Dirty_Bits_Entry4, Dirty_Bits_Entry5, Dirty_Bits_Entry6, Dirty_Bits_Entry7}),
    .Fetch_From_RAM(fetch_from_memory));
  RAM Main_MEM (.addr(Address_Input), .oe(fetch_from_memory), .clk(Clk_in), .dout(MEM_Data));  // open: we, din

  // Other names for the same wires on the sheet: Address[7:0] = Address_Input; Clkin = Clk_in;
  //   CPU_Data[7:0] = CPU_Input; Data_Out[7:0] = out_13;
  //   Dirty_Bits_0_to_7[7:0] = {Dirty_Bits_Entry0, Dirty_Bits_Entry1, Dirty_Bits_Entry2, DIrty_Bits_Entry3, Dirty_Bits_Entry4, Dirty_Bits_Entry5, Dirty_Bits_Entry6, Dirty_Bits_Entry7};
  //   TAGS[39:0] = {Entry7, Entry6, Entry5, Entry4, Entry3, Entry2, Entry1, Entry0};
  //   Valid_Bits_0_to7[7:0] = {Valid_Bits_Entry0, Valid_Bits_Entry1, Valid_Bits_Entry2, Valid_Bits_Entry3, Valid_Bits_Entry4, Valid_Bits_Entry5, Valid_Bits_Entry6, Valid_Bits_Entry7};
  //   Write_Data = Write_Enable

  // Notes on the sheet:
  //   Dity bits 0 - 7
  //   Input Value
  //   5 Bits
  //   Output Value
  //   Valid bits 0 - 7
  //   Cache Data Output
  //   Details:  8 bits address
  //   TAG: Upper 5 bits
  //   Index: Lower 3 bits
  //   Need Store The Data Is 2^8 = 256 Bits in RAM
  //   Offset: We don't need it, because 1 word per block
endmodule

module EightBitsCache (
  input  [7:0] Address_in,
  input  Write_Enable,
  input  RAM_Write_Enable,
  input  clk_in,
  input  [7:0] Data_in,
  output [39:0] Tag_out,
  output [7:0] Output_Data,
  output [7:0] Is_Entry_Valid,
  output [7:0] Dirty_Status,
  output Fetch_From_RAM
);

  wire and_1_out, and_5_out, Data_Write0, Data_Write1, Data_Write2, Data_Write3, Data_Write4, Data_Write5,
       Data_Write6, Data_Write7, Dirty_Write0, Dirty_Write1, Dirty_Write2, Dirty_Write3, Dirty_Write4,
       Dirty_Write5, Dirty_Write6, Dirty_Write7, DirtyBit, or_1_out, or_2_out, Reg_Write0, Reg_Write1,
       Reg_Write2, Reg_Write3, Reg_Write4, Reg_Write5, Reg_Write6, Reg_Write7, TAG_MATCH, Valid_Bit,
       Valid_Check, Valid_Write0, Valid_Write1, Valid_Write2, Valid_Write3, Valid_Write4, Valid_Write5,
       Valid_Write6, Valid_Write7;
  wire [4:0] Selected_Tag, xor_1_out;
  wire [7:0] DataReg0, DataReg1, DataReg2, DataReg3, DataReg4, DataReg5, DataReg6, DataReg7;

  Register #(.trigger("falling"), .width(5)) register_1 (
    .D(Address_in[7:3]), .en(Reg_Write0), .clk(clk_in), .Q(Tag_out[4:0]));  // open: clr
  Register #(.trigger("falling")) register_2 (.D(Data_in), .en(Data_Write0), .clk(clk_in), .Q(DataReg0));  // open: clr
  Register #(.trigger("falling")) register_3 (.D(Data_in), .en(Data_Write4), .clk(clk_in), .Q(DataReg4));  // open: clr
  Register #(.trigger("falling"), .width(1)) register_4 (
    .D(DirtyBit), .en(Dirty_Write0), .clk(clk_in), .Q(Dirty_Status[7]));  // open: clr
  Register #(.trigger("falling"), .width(1)) register_5 (
    .D(Valid_Bit), .en(Valid_Write0), .clk(clk_in), .Q(Is_Entry_Valid[7]));  // open: clr
  Register #(.trigger("falling"), .width(1)) register_6 (
    .D(Valid_Bit), .en(Valid_Write4), .clk(clk_in), .Q(Is_Entry_Valid[3]));  // open: clr
  Demultiplexer #(.select(3)) demultiplexer_1 (
    .out0(Reg_Write0), .out1(Reg_Write1), .out2(Reg_Write2), .out3(Reg_Write3), .out4(Reg_Write4),
    .out5(Reg_Write5), .out6(Reg_Write6), .out7(Reg_Write7), .in(RAM_Write_Enable), .sel(Address_in[2:0]));  // open: en
  Register #(.trigger("falling"), .width(5)) register_7 (
    .D(Address_in[7:3]), .en(Reg_Write4), .clk(clk_in), .Q(Tag_out[24:20]));  // open: clr
  and and_1 (and_1_out, TAG_MATCH, Write_Enable);
  and and_2 (DirtyBit, Write_Enable, TAG_MATCH);
  Register #(.trigger("falling"), .width(1)) register_8 (
    .D(DirtyBit), .en(Dirty_Write4), .clk(clk_in), .Q(Dirty_Status[3]));  // open: clr
  and and_3 (Valid_Bit, ~Write_Enable, ~Valid_Check);  // AND_Gate
  or or_1 (or_1_out, and_1_out, RAM_Write_Enable);
  or or_2 (or_2_out, RAM_Write_Enable, DirtyBit);
  Demultiplexer #(.select(3)) demultiplexer_2 (
    .out0(Dirty_Write0), .out1(Dirty_Write1), .out2(Dirty_Write2), .out3(Dirty_Write3), .out4(Dirty_Write4),
    .out5(Dirty_Write5), .out6(Dirty_Write6), .out7(Dirty_Write7), .in(or_2_out), .sel(Address_in[2:0]));  // open: en
  Demultiplexer #(.select(3)) demultiplexer_3 (
    .out0(Valid_Write0), .out1(Valid_Write1), .out2(Valid_Write2), .out3(Valid_Write3), .out4(Valid_Write4),
    .out5(Valid_Write5), .out6(Valid_Write6), .out7(Valid_Write7), .in(Valid_Bit), .sel(Address_in[2:0]));  // open: en
  Register #(.trigger("falling"), .width(5)) register_9 (
    .D(Address_in[7:3]), .en(Reg_Write1), .clk(clk_in), .Q(Tag_out[9:5]));  // open: clr
  Demultiplexer #(.select(3)) demultiplexer_4 (
    .out0(Data_Write0), .out1(Data_Write1), .out2(Data_Write2), .out3(Data_Write3), .out4(Data_Write4),
    .out5(Data_Write5), .out6(Data_Write6), .out7(Data_Write7), .in(or_1_out), .sel(Address_in[2:0]));  // open: en
  Register #(.trigger("falling"), .width(1)) register_10 (
    .D(DirtyBit), .en(Dirty_Write1), .clk(clk_in), .Q(Dirty_Status[6]));  // open: clr
  Register #(.trigger("falling"), .width(5)) register_11 (
    .D(Address_in[7:3]), .en(Reg_Write5), .clk(clk_in), .Q(Tag_out[29:25]));  // open: clr
  Register #(.trigger("falling")) register_12 (.D(Data_in), .en(Data_Write1), .clk(clk_in), .Q(DataReg1));  // open: clr
  Register #(.trigger("falling")) register_13 (.D(Data_in), .en(Data_Write5), .clk(clk_in), .Q(DataReg5));  // open: clr
  Register #(.trigger("falling"), .width(1)) register_14 (
    .D(DirtyBit), .en(Dirty_Write5), .clk(clk_in), .Q(Dirty_Status[2]));  // open: clr
  Register #(.trigger("falling"), .width(1)) register_15 (
    .D(Valid_Bit), .en(Valid_Write1), .clk(clk_in), .Q(Is_Entry_Valid[6]));  // open: clr
  Register #(.trigger("falling"), .width(1)) register_16 (
    .D(Valid_Bit), .en(Valid_Write5), .clk(clk_in), .Q(Is_Entry_Valid[2]));  // open: clr
  Register #(.trigger("falling"), .width(5)) register_17 (
    .D(Address_in[7:3]), .en(Reg_Write2), .clk(clk_in), .Q(Tag_out[14:10]));  // open: clr
  Register #(.trigger("falling"), .width(1)) register_18 (
    .D(DirtyBit), .en(Dirty_Write2), .clk(clk_in), .Q(Dirty_Status[5]));  // open: clr
  assign xor_1_out = Address_in[7:3] ^ Selected_Tag;  // XOR_Gate xor_1, 5 bits wide
  Register #(.trigger("falling"), .width(5)) register_19 (
    .D(Address_in[7:3]), .en(Reg_Write6), .clk(clk_in), .Q(Tag_out[34:30]));  // open: clr
  Register #(.trigger("falling"), .width(1)) register_20 (
    .D(DirtyBit), .en(Dirty_Write6), .clk(clk_in), .Q(Dirty_Status[1]));  // open: clr
  Register #(.trigger("falling"), .width(1)) register_21 (
    .D(Valid_Bit), .en(Valid_Write2), .clk(clk_in), .Q(Is_Entry_Valid[5]));  // open: clr
  Register #(.trigger("falling"), .width(1)) register_22 (
    .D(Valid_Bit), .en(Valid_Write6), .clk(clk_in), .Q(Is_Entry_Valid[1]));  // open: clr
  and and_4 (Fetch_From_RAM, ~Write_Enable, ~TAG_MATCH);  // AND_Gate
  Register #(.trigger("falling")) register_23 (.D(Data_in), .en(Data_Write2), .clk(clk_in), .Q(DataReg2));  // open: clr
  Register #(.trigger("falling")) register_24 (.D(Data_in), .en(Data_Write6), .clk(clk_in), .Q(DataReg6));  // open: clr
  and and_5 (and_5_out, ~xor_1_out[0], ~xor_1_out[1], ~xor_1_out[2], ~xor_1_out[3], ~xor_1_out[4]);  // AND_Gate
  and and_6 (TAG_MATCH, and_5_out, Valid_Check);
  Register #(.trigger("falling"), .width(5)) register_25 (
    .D(Address_in[7:3]), .en(Reg_Write3), .clk(clk_in), .Q(Tag_out[19:15]));  // open: clr
  Register #(.trigger("falling"), .width(1)) register_26 (
    .D(DirtyBit), .en(Dirty_Write3), .clk(clk_in), .Q(Dirty_Status[4]));  // open: clr
  Multiplexer #(.select(3)) multiplexer_1 (
    .in0(Is_Entry_Valid[7]), .in1(Is_Entry_Valid[6]), .in2(Is_Entry_Valid[5]), .in3(Is_Entry_Valid[4]),
    .in4(Is_Entry_Valid[3]), .in5(Is_Entry_Valid[2]), .in6(Is_Entry_Valid[1]), .in7(Is_Entry_Valid[0]),
    .out(Valid_Check), .sel(Address_in[2:0]));  // open: en
  Register #(.trigger("falling"), .width(5)) register_27 (
    .D(Address_in[7:3]), .en(Reg_Write7), .clk(clk_in), .Q(Tag_out[39:35]));  // open: clr
  Register #(.trigger("falling"), .width(1)) register_28 (
    .D(DirtyBit), .en(Dirty_Write7), .clk(clk_in), .Q(Dirty_Status[0]));  // open: clr
  Register #(.trigger("falling"), .width(1)) register_29 (
    .D(Valid_Bit), .en(Valid_Write3), .clk(clk_in), .Q(Is_Entry_Valid[4]));  // open: clr
  Register #(.trigger("falling"), .width(1)) register_30 (
    .D(Valid_Bit), .en(Valid_Write7), .clk(clk_in), .Q(Is_Entry_Valid[0]));  // open: clr
  Register #(.trigger("falling")) register_31 (.D(Data_in), .en(Data_Write3), .clk(clk_in), .Q(DataReg3));  // open: clr
  Register #(.trigger("falling")) register_32 (.D(Data_in), .en(Data_Write7), .clk(clk_in), .Q(DataReg7));  // open: clr
  Multiplexer #(.select(3), .width(5)) multiplexer_2 (
    .in0(Tag_out[4:0]), .in1(Tag_out[9:5]), .in2(Tag_out[14:10]), .in3(Tag_out[19:15]), .in4(Tag_out[24:20]),
    .in5(Tag_out[29:25]), .in6(Tag_out[34:30]), .in7(Tag_out[39:35]), .out(Selected_Tag),
    .sel(Address_in[2:0]));  // open: en
  Multiplexer #(.select(3), .width(8)) multiplexer_3 (
    .in0(DataReg0), .in1(DataReg1), .in2(DataReg2), .in3(DataReg3), .in4(DataReg4), .in5(DataReg5),
    .in6(DataReg6), .in7(DataReg7), .out(Output_Data), .sel(Address_in[2:0]));  // open: en

  // Other names for the same wires on the sheet: ENTRY[2:0] = Address_in[2:0]; Data_Tag[4:0] = Address_in[7:3];
  //   clk = clk_in; Data_Data[7:0] = Data_in; Data_OUT[7:0] = Output_Data; DIRTY_OUT[7:0] = Dirty_Status;
  //   DirtyBit7 = Dirty_Status[0]; DirtyBit6 = Dirty_Status[1]; DirtyBit5 = Dirty_Status[2];
  //   DirtyBit4 = Dirty_Status[3]; DirtyBit3 = Dirty_Status[4]; DirtyBit2 = Dirty_Status[5];
  //   DirtyBit1 = Dirty_Status[6]; DirtyBit0 = Dirty_Status[7]; mem_update = Fetch_From_RAM;
  //   Mem_Write = RAM_Write_Enable; Reg_Write = Write_Enable; Reg0[4:0] = Tag_out[4:0]; Reg1[4:0] = Tag_out[9:5];
  //   Reg2[4:0] = Tag_out[14:10]; Reg3[4:0] = Tag_out[19:15]; Reg4[4:0] = Tag_out[24:20]; Reg5[4:0] = Tag_out[29:25];
  //   Reg6[4:0] = Tag_out[34:30]; Reg7[4:0] = Tag_out[39:35]; Valid_OUT[7:0] = Is_Entry_Valid;
  //   ValidBit7 = Is_Entry_Valid[0]; ValidBit6 = Is_Entry_Valid[1]; ValidBit5 = Is_Entry_Valid[2];
  //   ValidBit4 = Is_Entry_Valid[3]; ValidBit3 = Is_Entry_Valid[4]; ValidBit2 = Is_Entry_Valid[5];
  //   ValidBit1 = Is_Entry_Valid[6]; ValidBit0 = Is_Entry_Valid[7]

  // Notes on the sheet:
  //   The Values input
  //   Memory Write Register Control
  //   Dity Bits Controls
  //   Valid Bits Control Area
  //   The Values Output
  //   Update : Fetch From RAM
  //   Check The Match Tag and Validations
  //   if ( incoming_Tags == Current_Selects_Tags) ??
  //   Validation Check
  //   1: Entry Is Contail Valid and Usable Data || 0: Does Not Contain Valid 
endmodule
