// Logisim project VedningMachine.circ as structural Verilog: 4 circuits, main circuit FSV
module main (
  input  Dime,
  input  Nikel,
  output [1:0] out_3
);

  wire and_1_out, and_2_out, and_3_out, and_4_out, and_5_out, and_6_out, and_7_out, and_8_out, Clk,
       not_1_out, not_2_out, not_3_out, not_4_out, or_1_out, or_2_out, y1_q, y2_q, y2_qn;

  not not_1 (not_1_out, Dime);
  not not_2 (not_2_out, Nikel);
  Clock clock_1 (.out(Clk));
  and and_1 (and_1_out, Nikel, not_4_out);
  and and_2 (and_2_out, Dime, not_3_out);
  and and_3 (and_3_out, Dime, not_3_out, y2_q);
  and and_4 (and_4_out, y2_q, Nikel, not_3_out);
  and and_5 (and_5_out, not_2_out, not_1_out, y2_q);
  and and_6 (and_6_out, not_1_out, not_2_out, y1_q);
  not not_3 (not_3_out, y1_q);
  or or_1 (or_1_out, and_3_out, and_1_out, and_5_out);
  not not_4 (not_4_out, y2_q);
  or or_2 (or_2_out, and_4_out, and_2_out, and_6_out);
  D_Flip_Flop y1 (.D(or_2_out), .clk(Clk), .Q(y1_q));  // open: Qn, preset, reset
  D_Flip_Flop y2 (.D(or_1_out), .clk(Clk), .Q(y2_q), .Qn(y2_qn));  // open: preset, reset
  and and_7 (and_7_out, Dime, y1_q);
  and and_8 (and_8_out, y1_q, y2_q, Nikel);
  and and_9 (out_3[0], y1_q, y2_q, Dime);
  or or_3 (out_3[1], and_7_out, and_8_out);

  // Notes on the sheet:
  //   x1
  //   x2
  //   y1
  //   !y1
  //   y2
  //   !y2
  //   z1
  //   z2
endmodule

module MonyCollectionBank (
  input  S5,
  input  S10,
  input  Clk,
  input  S25,
  input  Enable,
  input  Reset,
  output [7:0] AcctSum,
  output [1:0] out_8,
  output [7:0] out_9
);

  wire CoinIn;
  wire [7:0] adder_1_out;

  or or_1 (CoinIn, S5, S10, S25);
  Priority_Encoder #(.select(2)) priority_encoder_1 (
    .in0(1'b1), .in1(S5), .in2(S10), .in3(S25), .out(out_8), .en_in(Enable));  // open: gs, en_out
  Multiplexer #(.enable("false"), .select(2), .width(8)) multiplexer_1 (
    .in0({8{1'b0}}), .in1(8'h5), .in2(8'ha), .in3(8'h19), .out(out_9), .sel(out_8));
  Adder adder_1 (.a(AcctSum), .b(out_9), .out(adder_1_out));  // open: cin, cout
  Register register_1 (.D(adder_1_out), .en(Enable), .clk(Clk), .Q(AcctSum), .clr(Reset));

  // Other names for the same wires on the sheet: En = Enable; In5 = S5; In10 = S10; In25 = S25; Rest = Reset

  // Notes on the sheet:
  //   There has the issues
endmodule

module FSV (
  input  Enable,
  input  Nikel,
  input  Dime,
  input  Quarter,
  input  Reset,
  output [7:0] Testing,
  output [11:0] TotalAmount,
  output [11:0] out_8,
  output OutputSignal
);

  wire Clk_out;

  Clock Clk (.out(Clk_out));
  MonyCollectionBank monycollectionbank_1 (
    .S5(Nikel), .S10(Dime), .Clk(Clk_out), .S25(Quarter), .Enable(Enable), .Reset(Reset), .AcctSum(Testing));  // open: out_8, out_9
  Changed changed_1 (.CashIn(Testing), .DepostieAmount(TotalAmount), .ChangedAmount(out_8), .Activator(OutputSignal));
endmodule

module Changed (
  input  [7:0] CashIn,
  output [11:0] DepostieAmount,
  output [11:0] ChangedAmount,
  output Activator
);

  wire comparator_1_eq, comparator_1_gt;
  wire [7:0] multiplexer_1_out, subtractor_1_out;

  // Binairy_to_BCD_converter #(.binvalue(8)) binairy_to_bcd_converter_1: pin names not known; wires that end beside it: CashIn, DepostieAmount[11:8], DepostieAmount[7:4], DepostieAmount[3:0]
  Comparator comparator_1 (.a(CashIn), .b(8'h4b), .gt(comparator_1_gt), .eq(comparator_1_eq));  // open: lt
  Multiplexer #(.enable("false"), .width(8)) multiplexer_1 (
    .in0(8'h4b), .in1(CashIn), .out(multiplexer_1_out), .sel(comparator_1_gt));
  Subtractor subtractor_1 (.a(multiplexer_1_out), .b(8'h4b), .out(subtractor_1_out));  // open: bin, bout
  or or_1 (Activator, comparator_1_gt, comparator_1_eq);
  // Binairy_to_BCD_converter #(.binvalue(8)) binairy_to_bcd_converter_2: pin names not known; wires that end beside it: subtractor_1_out, ChangedAmount[11:8], ChangedAmount[7:4], ChangedAmount[3:0]

  // Notes on the sheet:
  //   4b -> 8 bits machine -> 64 + 1 1 = 75 decimal
endmodule
